// Logisim project CS 200 - Project 1.circ as structural Verilog: 1 circuit, main circuit main
module main (
  input  Cin,
  input  X2,
  input  X1,
  input  X0,
  input  Y2,
  input  Y1,
  input  Y0,
  output Cout,
  output Sum,
  output Sum_2,
  output Sum_3
);

  wire and_1_out, and_2_out, and_3_out, and_4_out, and_5_out, and_6_out, and_7_out, and_8_out, and_9_out,
       and_10_out, and_11_out, and_12_out, and_13_out, and_14_out, and_15_out, and_16_out, and_17_out,
       and_18_out, and_19_out, and_20_out, and_21_out, not_1_out, not_2_out, not_3_out, not_4_out, not_5_out,
       not_6_out, not_7_out, not_8_out, not_9_out, or_4_out, or_6_out;

  not not_1 (not_1_out, Y2);
  not not_2 (not_2_out, or_4_out);
  not not_3 (not_3_out, X2);
  and and_1 (and_1_out, not_2_out, not_3_out, Y2);
  and and_2 (and_2_out, not_2_out, X2, not_1_out);
  and and_3 (and_3_out, or_4_out, not_3_out, not_1_out);
  and and_4 (and_4_out, or_4_out, X2, Y2);
  and and_5 (and_5_out, or_4_out, Y2);
  and and_6 (and_6_out, X2, Y2);
  and and_7 (and_7_out, or_4_out, X2);
  or or_1 (Sum, and_1_out, and_2_out, and_3_out, and_4_out);
  or or_2 (Cout, and_5_out, and_6_out, and_7_out);
  not not_4 (not_4_out, Y1);
  not not_5 (not_5_out, X1);
  not not_6 (not_6_out, or_6_out);
  and and_8 (and_8_out, not_6_out, not_5_out, Y1);
  and and_9 (and_9_out, not_6_out, X1, not_4_out);
  and and_10 (and_10_out, or_6_out, not_5_out, not_4_out);
  and and_11 (and_11_out, or_6_out, X1, Y1);
  and and_12 (and_12_out, or_6_out, Y1);
  and and_13 (and_13_out, X1, Y1);
  and and_14 (and_14_out, or_6_out, X1);
  or or_3 (Sum_2, and_8_out, and_9_out, and_10_out, and_11_out);
  or or_4 (or_4_out, and_12_out, and_13_out, and_14_out);
  not not_7 (not_7_out, X0);
  not not_8 (not_8_out, Y0);
  not not_9 (not_9_out, Cin);
  and and_15 (and_15_out, not_9_out, not_7_out, Y0);
  and and_16 (and_16_out, not_9_out, X0, not_8_out);
  and and_17 (and_17_out, Cin, not_7_out, not_8_out);
  and and_18 (and_18_out, Cin, X0, Y0);
  and and_19 (and_19_out, Cin, Y0);
  and and_20 (and_20_out, X0, Y0);
  and and_21 (and_21_out, Cin, X0);
  or or_5 (Sum_3, and_15_out, and_16_out, and_17_out, and_18_out);
  or or_6 (or_6_out, and_19_out, and_20_out, and_21_out);
endmodule
