// Logisim project CS 200 - Project 2.circ as structural Verilog: 9 circuits, main circuit Counter
module main (
  input  in_1,
  input  Clk,
  output D,
  output C,
  output B,
  output A
);

  wire and_1_out, and_2_out, and_3_out, and_4_out, and_5_out, or_1_out;

  and and_1 (and_1_out, in_1, D);
  and and_2 (and_2_out, and_1_out, C);
  and and_3 (and_3_out, and_2_out, B);
  J_K_Flip_Flop j_k_ff_1 (.J(in_1), .clk(Clk), .K(in_1), .Q(D), .reset(or_1_out));  // open: Qn, preset, en
  J_K_Flip_Flop j_k_ff_2 (.J(and_1_out), .clk(Clk), .K(and_1_out), .Q(C), .reset(or_1_out));  // open: Qn, preset, en
  J_K_Flip_Flop j_k_ff_3 (.J(and_2_out), .clk(Clk), .K(and_2_out), .Q(B), .reset(or_1_out));  // open: Qn, preset, en
  J_K_Flip_Flop j_k_ff_4 (.J(and_3_out), .clk(Clk), .K(and_3_out), .Q(A), .reset(or_1_out));  // open: Qn, preset, en
  and and_4 (and_4_out, C, A);
  and and_5 (and_5_out, B, A);
  or or_1 (or_1_out, and_5_out, and_4_out);
endmodule

module Counter (
);

  wire button_1_out, Main_a, Main_b, Main_c, Main_d, Seg_0_out_5, Seg_1_out_5, Seg_2_out_5, Seg_3_out_5,
       Seg_4_out_5, Seg_5_out_5, Seg_6_out_5;

  Button button_1 (.out(button_1_out));
  main Main (.in_1(1'b1), .Clk(button_1_out), .D(Main_d), .C(Main_c), .B(Main_b), .A(Main_a));
  LED led_1 (.in(Main_a));
  LED led_2 (.in(Main_b));
  LED led_3 (.in(Main_c));
  LED led_4 (.in(Main_d));
  seg_1 Seg_1 (.A(Main_a), .B(Main_b), .C(Main_c), .D(Main_d), .out_5(Seg_1_out_5));
  Seg_2 Seg_2 (.A(Main_a), .B(Main_b), .C(Main_c), .D(Main_d), .out_5(Seg_2_out_5));
  seg_3 Seg_3 (.A(Main_a), .B(Main_b), .C(Main_c), .D(Main_d), .out_5(Seg_3_out_5));
  Seg_4 Seg_4 (.A(Main_a), .B(Main_b), .C(Main_c), .D(Main_d), .out_5(Seg_4_out_5));
  Seg_5 Seg_5 (.A(Main_a), .B(Main_b), .C(Main_c), .D(Main_d), .out_5(Seg_5_out_5));
  Seg_6 Seg_6 (.A(Main_a), .B(Main_b), .C(Main_c), .D(Main_d), .out_5(Seg_6_out_5));
  seg_0 Seg_0 (.A(Main_a), .B(Main_b), .C(Main_c), .D(Main_d), .out_5(Seg_0_out_5));
  _7_Segment_Display u_7_segment_display_1 (
    .g(Seg_6_out_5), .f(Seg_3_out_5), .a(Seg_2_out_5), .b(Seg_1_out_5), .e(Seg_4_out_5), .d(Seg_5_out_5),
    .c(Seg_0_out_5));  // open: dp

  // Notes on the sheet:
  //   Clk
  //   B
  //   A
  //   D
  //   C
endmodule

module seg_0 (
  input  A,
  input  B,
  input  C,
  input  D,
  output out_5
);

  or or_1 (out_5, A, B, ~C, D);  // OR_Gate
endmodule

module seg_1 (
  input  A,
  input  B,
  input  C,
  input  D,
  output out_5
);

  wire c_prime_d_prime_out, cd_out;

  and c_prime_d_prime (c_prime_d_prime_out, ~D, ~C);  // AND_Gate
  and cd (cd_out, D, C);
  or a_b_prime (out_5, c_prime_d_prime_out, A, ~B, cd_out);  // OR_Gate
endmodule

module seg_3 (
  input  A,
  input  B,
  input  C,
  input  D,
  output out_5
);

  wire bc_prime_out, bd_prime_out, c_prime_d_prime_out;

  and c_prime_d_prime (c_prime_d_prime_out, ~C, ~D);  // AND_Gate
  and bc_prime (bc_prime_out, B, ~C);  // AND_Gate
  and bd_prime (bd_prime_out, B, ~D);  // AND_Gate
  or or_1 (out_5, A, c_prime_d_prime_out, bc_prime_out, bd_prime_out);
endmodule

module Seg_2 (
  input  A,
  input  B,
  input  C,
  input  D,
  output out_5
);

  wire b_prime_d_prime_out, bd_out;

  and b_prime_d_prime (b_prime_d_prime_out, ~B, ~D);  // AND_Gate
  and bd (bd_out, B, D);
  or or_1 (out_5, b_prime_d_prime_out, A, C, bd_out);
endmodule

module Seg_4 (
  input  A,
  input  B,
  input  C,
  input  D,
  output out_5
);

  wire ab_out, ac_out, b_prime_d_prime_out, cd_prime_out;

  and b_prime_d_prime (b_prime_d_prime_out, ~B, ~D);  // AND_Gate
  and ab (ab_out, A, B);
  and ac (ac_out, A, C);
  and cd_prime (cd_prime_out, C, ~D);  // AND_Gate
  or or_1 (out_5, b_prime_d_prime_out, ab_out, ac_out, cd_prime_out);
endmodule

module Seg_5 (
  input  A,
  input  B,
  input  C,
  input  D,
  output out_5
);

  wire b_prime_c_out, b_prime_d_prime_out, bc_prime_d_out, cd_prime_out;

  and bc_prime_d (bc_prime_d_out, B, ~C, D);  // AND_Gate
  and b_prime_d_prime (b_prime_d_prime_out, ~B, ~D);  // AND_Gate
  and b_prime_c (b_prime_c_out, ~B, C);  // AND_Gate
  and cd_prime (cd_prime_out, C, ~D);  // AND_Gate
  or or_1 (out_5, A, bc_prime_d_out, b_prime_d_prime_out, b_prime_c_out, cd_prime_out);

  // Notes on the sheet:
  //   This one was way silly hard to wire up. LOL
endmodule

module Seg_6 (
  input  A,
  input  B,
  input  C,
  input  D,
  output out_5
);

  wire b_prime_c_out, bc_prime_out, bd_prime_out;

  and b_prime_c (b_prime_c_out, ~B, C);  // AND_Gate
  and bc_prime (bc_prime_out, B, ~C);  // AND_Gate
  and bd_prime (bd_prime_out, B, ~D);  // AND_Gate
  or or_1 (out_5, A, b_prime_c_out, bc_prime_out, bd_prime_out);
endmodule
